// Logisim project TimedLab1.circ as structural Verilog: 1 circuit, main circuit 4 Bit ALU
module _4_Bit_ALU (
  input  [3:0] in_1,
  input  [3:0] in_2,
  input  [1:0] in_3,
  output [3:0] out_4
);

  wire [3:0] and_1_out, and_2_out, nand_1_out, or_1_out;

  assign and_1_out = ~in_1 & in_2;  // AND_Gate and_1, 4 bits wide
  assign and_2_out = in_1 & ~in_2;  // AND_Gate and_2, 4 bits wide
  assign nand_1_out = ~(~in_1 & ~in_2);  // NAND_Gate nand_1, 4 bits wide
  assign or_1_out = and_1_out | and_2_out;  // OR_Gate or_1, 4 bits wide
  Multiplexer #(.select(2), .width(4), .disabled(0), .enable("false")) multiplexer_1 (
    .in0(nand_1_out), .in1({3'b000, in_1[0]}), .in2({{2{in_1[3]}}, in_1[2:1]}), .in3(or_1_out), .out(out_4),
    .sel(in_3));

  // Other names for the same wires on the sheet: A[3:0] = in_1; B[3:0] = in_2

  // Notes on the sheet:
  //   OP-CODE
  //   00-OR
  //   01-MODULUS
  //   10-RIGHT SHIFT
  //   11-XOR
endmodule
