// Logisim project hw3.circ as structural Verilog: 5 circuits, main circuit 16-bit ALU
module _1_bit_full_adder (
  input  Input_A,
  input  Input_B,
  input  CarryIn,
  output CarryOut,
  output Answer
);

  wire and_2_out, and_3_out, and_4_out, and_5_out, and_6_out, and_7_out, and_8_out, not_1_out, not_2_out,
       not_3_out, not_4_out, not_5_out, not_6_out, not_7_out, not_8_out, not_9_out, not_10_out, not_11_out,
       not_12_out;

  not not_1 (not_1_out, Input_A);
  not not_2 (not_2_out, Input_B);
  not not_3 (not_3_out, CarryIn);
  not not_4 (not_4_out, Input_A);
  not not_5 (not_5_out, Input_B);
  not not_6 (not_6_out, Input_A);
  not not_7 (not_7_out, CarryIn);
  not not_8 (not_8_out, Input_A);
  not not_9 (not_9_out, Input_B);
  not not_10 (not_10_out, CarryIn);
  not not_11 (not_11_out, Input_B);
  not not_12 (not_12_out, CarryIn);
  // AND_Gate and_1 has open pins: in0=not_1_out, in1=not_2_out, in2=not_3_out, out=open
  and and_2 (and_2_out, not_4_out, not_5_out, CarryIn);
  and and_3 (and_3_out, not_6_out, Input_B, not_7_out);
  and and_4 (and_4_out, not_8_out, Input_B, CarryIn);
  and and_5 (and_5_out, Input_A, not_9_out, not_10_out);
  and and_6 (and_6_out, Input_A, not_11_out, CarryIn);
  and and_7 (and_7_out, Input_A, Input_B, not_12_out);
  and and_8 (and_8_out, Input_A, Input_B, CarryIn);
  or or_1 (CarryOut, and_4_out, and_6_out, and_7_out, and_8_out);
  or or_2 (Answer, and_2_out, and_3_out, and_5_out, and_8_out);
endmodule

module _4_bit_full_adder (
  input  [3:0] A,
  input  [3:0] B,
  input  Carry_In,
  output Carry_Out,
  output [3:0] out_5
);

  wire n1_bit_full_adder_1_answer, n1_bit_full_adder_2_answer, n1_bit_full_adder_3_answer;

  _1_bit_full_adder u_1_bit_full_adder_1 (
    .Input_A(A[0]), .Input_B(B[0]), .CarryIn(Carry_In), .CarryOut(out_5[0]),
    .Answer(n1_bit_full_adder_1_answer));
  _1_bit_full_adder u_1_bit_full_adder_2 (
    .Input_A(A[1]), .Input_B(B[1]), .CarryIn(n1_bit_full_adder_1_answer), .CarryOut(out_5[1]),
    .Answer(n1_bit_full_adder_2_answer));
  _1_bit_full_adder u_1_bit_full_adder_3 (
    .Input_A(A[2]), .Input_B(B[2]), .CarryIn(n1_bit_full_adder_2_answer), .CarryOut(out_5[2]),
    .Answer(n1_bit_full_adder_3_answer));
  _1_bit_full_adder u_1_bit_full_adder_4 (
    .Input_A(A[3]), .Input_B(B[3]), .CarryIn(n1_bit_full_adder_3_answer), .CarryOut(out_5[3]),
    .Answer(Carry_Out));

  // Notes on the sheet:
  //   0
  //   Answer
  //   1
  //   2
  //   3
endmodule

module _4_bit_ALU (
  input  [3:0] A,
  input  [3:0] B,
  input  S0,
  input  S1,
  input  S2,
  output [3:0] Result
);

  wire [3:0] and_1_out, n4_bit_full_adder_1_out_5, n4_bit_full_adder_2_out_5, n4_bit_full_adder_3_out_5,
       n4_bit_full_adder_4_out_5, not_1_out, not_2_out, or_1_out, xor_1_out;

  assign not_1_out = ~B;  // NOT_Gate not_1, 4 bits wide
  _4_bit_full_adder u_4_bit_full_adder_1 (
    .A(A), .B(4'b1111), .Carry_In(1'b0), .out_5(n4_bit_full_adder_1_out_5));  // open: Carry_Out
  _4_bit_full_adder u_4_bit_full_adder_2 (
    .A(A), .B(B), .Carry_In(1'b0), .out_5(n4_bit_full_adder_2_out_5));  // open: Carry_Out
  _4_bit_full_adder u_4_bit_full_adder_3 (
    .A(A), .B(not_1_out), .Carry_In(1'b1), .out_5(n4_bit_full_adder_3_out_5));  // open: Carry_Out
  _4_bit_full_adder u_4_bit_full_adder_4 (
    .A(A), .B(4'b1111), .Carry_In(1'b0), .out_5(n4_bit_full_adder_4_out_5));  // open: Carry_Out
  assign not_2_out = ~n4_bit_full_adder_1_out_5;  // NOT_Gate not_2, 4 bits wide
  assign and_1_out = A & B;  // AND_Gate and_1, 4 bits wide
  assign or_1_out = A | B;  // OR_Gate or_1, 4 bits wide
  assign xor_1_out = A ^ B;  // XOR_Gate xor_1, 4 bits wide
  Multiplexer #(.select(3), .width(4), .disabled(0), .enable("false")) multiplexer_1 (
    .in0(n4_bit_full_adder_2_out_5), .in1(n4_bit_full_adder_3_out_5), .in2(n4_bit_full_adder_4_out_5),
    .in3(not_2_out), .in4({A[1:0], 2'b00}), .in5(and_1_out), .in6(or_1_out), .in7(xor_1_out), .out(Result),
    .sel({S2, S1, S0}));

  // Notes on the sheet:
  //   000-ADD
  //   001-SUB
  //   101-AND
  //   110-OR
  //   111-XOR
  //   OP-CODE
  //   010-DECREMENT
  //   011-NEGATION
  //   100-MULTIPLICATION (BY 4)
endmodule

module _16_bit_full_adder (
  input  [15:0] A,
  input  [15:0] B,
  input  Carry_In,
  output Carry_Out,
  output [15:0] Sum
);

  wire n4_bit_full_adder_1_carry_out, n4_bit_full_adder_2_carry_out, n4_bit_full_adder_3_carry_out;

  _4_bit_full_adder u_4_bit_full_adder_1 (
    .A(A[3:0]), .B(B[3:0]), .Carry_In(Carry_In), .Carry_Out(n4_bit_full_adder_1_carry_out), .out_5(Sum[3:0]));
  _4_bit_full_adder u_4_bit_full_adder_2 (
    .A(A[7:4]), .B(B[7:4]), .Carry_In(n4_bit_full_adder_1_carry_out),
    .Carry_Out(n4_bit_full_adder_2_carry_out), .out_5(Sum[7:4]));
  _4_bit_full_adder u_4_bit_full_adder_3 (
    .A(A[11:8]), .B(B[11:8]), .Carry_In(n4_bit_full_adder_2_carry_out),
    .Carry_Out(n4_bit_full_adder_3_carry_out), .out_5(Sum[11:8]));
  _4_bit_full_adder u_4_bit_full_adder_4 (
    .A(A[15:12]), .B(B[15:12]), .Carry_In(n4_bit_full_adder_3_carry_out), .Carry_Out(Carry_Out),
    .out_5(Sum[15:12]));

  // Notes on the sheet:
  //   0
  //   1
  //   2
  //   3
endmodule

module _16_bit_ALU (
  input  [15:0] A,
  input  [15:0] B,
  input  S0,
  input  S1,
  input  S2,
  output [15:0] Result
);

  wire [15:0] and_1_out, n16_bit_full_adder_1_sum, n16_bit_full_adder_2_sum, n16_bit_full_adder_3_sum,
       n16_bit_full_adder_4_sum, not_1_out, not_2_out, or_1_out, xor_1_out;

  assign not_1_out = ~B;  // NOT_Gate not_1, 16 bits wide
  _16_bit_full_adder u_16_bit_full_adder_1 (
    .A(A), .B({16{1'b1}}), .Carry_In(1'b0), .Sum(n16_bit_full_adder_1_sum));  // open: Carry_Out
  _16_bit_full_adder u_16_bit_full_adder_2 (
    .A(A), .B(B), .Carry_In(1'b0), .Sum(n16_bit_full_adder_2_sum));  // open: Carry_Out
  _16_bit_full_adder u_16_bit_full_adder_3 (
    .A(A), .B(not_1_out), .Carry_In(1'b1), .Sum(n16_bit_full_adder_3_sum));  // open: Carry_Out
  _16_bit_full_adder u_16_bit_full_adder_4 (
    .A(A), .B({16{1'b1}}), .Carry_In(1'b0), .Sum(n16_bit_full_adder_4_sum));  // open: Carry_Out
  assign not_2_out = ~n16_bit_full_adder_1_sum;  // NOT_Gate not_2, 16 bits wide
  assign and_1_out = A & B;  // AND_Gate and_1, 16 bits wide
  assign or_1_out = A | B;  // OR_Gate or_1, 16 bits wide
  assign xor_1_out = A ^ B;  // XOR_Gate xor_1, 16 bits wide
  Multiplexer #(.select(3), .width(16), .disabled(0), .enable("false")) multiplexer_1 (
    .in0(n16_bit_full_adder_2_sum), .in1(n16_bit_full_adder_3_sum), .in2(n16_bit_full_adder_4_sum),
    .in3(not_2_out), .in4({A[1:0], {14{1'b0}}}), .in5(and_1_out), .in6(or_1_out), .in7(xor_1_out),
    .out(Result), .sel({S2, S1, S0}));

  // Notes on the sheet:
  //   000-ADD
  //   001-SUB
  //   101-AND
  //   110-OR
  //   111-XOR
  //   OP-CODE
  //   010-DECREMENT
  //   011-NEGATION
  //   100-MULTIPLICATION (BY 4)
endmodule
