// Logisim project hw4part1.circ as structural Verilog: 2 circuits, main circuit One Hot State Machine
module One_Hot_State_Machine (
  input  G,
  input  Clock,
  input  Reset,
  output W,
  output X,
  output Y,
  output Z
);

  wire and_1_out, and_2_out, and_3_out, and_4_out, and_5_out, and_6_out, and_7_out, and_10_out, C0, C1, C2,
       C3, C4, C5, C6, nor_1_out, or_1_out;
  wire [6:0] or_2_out;

  and and_1 (and_1_out, C0, ~G);  // AND_Gate
  and and_2 (and_2_out, C6, ~G);  // AND_Gate
  and and_3 (and_3_out, C0, G);
  and and_4 (and_4_out, C3, ~G);  // AND_Gate
  and and_5 (and_5_out, C1, G);
  and and_6 (and_6_out, C4, ~G);  // AND_Gate
  and and_7 (and_7_out, C1, ~G);  // AND_Gate
  and and_8 (or_2_out[4], C3, G);
  and and_9 (or_2_out[5], C4, G);
  and and_10 (and_10_out, C6, G);
  or or_1 (or_1_out, and_1_out, and_2_out);
  nor nor_1 (nor_1_out, C0, C1, C2, C3, C4, C5, C6);
  or or_2 (or_2_out[0], or_1_out, nor_1_out);
  or or_3 (or_2_out[1], and_3_out, and_4_out);
  or or_4 (or_2_out[2], and_5_out, and_6_out);
  or or_5 (or_2_out[3], and_7_out, C2);
  or or_6 (or_2_out[6], and_10_out, C5);
  Register #(.width(7)) register_1 (
    .D(or_2_out), .en(1'b1), .Q({C6, C5, C4, C3, C2, C1, C0}), .clk(Clock), .clr(Reset));
  or or_7 (W, C0, C3, C5);
  or or_8 (X, C3, C6);
  or or_9 (Y, C2, C3, C4, C5);
  or or_10 (Z, C4, C6);

  // Other names for the same wires on the sheet: CLK = Clock; RST = Reset

  // Notes on the sheet:
  //   My name is:
  //   [HONGRUI ZHENG]
  //   and this is my one-hot machine
endmodule

module Tester (
  input  G
);

  wire CLK_out, one_hot_state_machine_1_w, one_hot_state_machine_1_x, one_hot_state_machine_1_y,
       one_hot_state_machine_1_z, RST_out;

  Clock CLK (.out(CLK_out));
  LED led_1 (.in(one_hot_state_machine_1_w));
  One_Hot_State_Machine one_hot_state_machine_1 (
    .G(G), .Clock(CLK_out), .Reset(RST_out), .W(one_hot_state_machine_1_w), .X(one_hot_state_machine_1_x),
    .Y(one_hot_state_machine_1_y), .Z(one_hot_state_machine_1_z));
  LED led_2 (.in(one_hot_state_machine_1_x));
  LED led_3 (.in(one_hot_state_machine_1_y));
  LED led_4 (.in(one_hot_state_machine_1_z));
  Button RST (.out(RST_out));
endmodule
