// Logisim project hw4part2.circ as structural Verilog: 2 circuits, main circuit Tester
module Tester (
  input  G
);

  wire CLK_out, reduced_state_machine_1_w, reduced_state_machine_1_x, reduced_state_machine_1_y,
       reduced_state_machine_1_z, RST_out;

  Clock CLK (.out(CLK_out));
  Reduced_State_Machine reduced_state_machine_1 (
    .G(G), .Clock(CLK_out), .Reset(RST_out), .W(reduced_state_machine_1_w), .X(reduced_state_machine_1_x),
    .Y(reduced_state_machine_1_y), .Z(reduced_state_machine_1_z));
  LED led_1 (.in(reduced_state_machine_1_w));
  LED led_2 (.in(reduced_state_machine_1_x));
  LED led_3 (.in(reduced_state_machine_1_y));
  LED led_4 (.in(reduced_state_machine_1_z));
  Button RST (.out(RST_out));
endmodule

module Reduced_State_Machine (
  input  G,
  input  Clock,
  input  Reset,
  output W,
  output X,
  output Y,
  output Z
);

  wire _0, _1, _2, and_1_out, and_2_out, and_3_out, and_4_out, and_5_out, and_6_out, and_7_out, and_8_out,
       and_9_out, and_10_out, and_11_out, and_12_out, and_13_out, and_14_out, and_15_out, and_16_out,
       and_17_out;
  wire [2:0] or_1_out;

  and and_1 (and_1_out, ~G, _2, _0);  // AND_Gate
  and and_2 (and_2_out, ~_0, ~_2, _1);  // AND_Gate
  and and_3 (and_3_out, ~_0, ~_1, G);  // AND_Gate
  and and_4 (and_4_out, ~_1, _0);  // AND_Gate
  and and_5 (and_5_out, ~G, ~_1, _2);  // AND_Gate
  and and_6 (and_6_out, G, _2, _1);
  and and_7 (and_7_out, ~_2, ~_0, _1);  // AND_Gate
  and and_8 (and_8_out, G, _1, _0);
  and and_9 (and_9_out, G, _2);
  and and_10 (and_10_out, _0, _2);
  or or_1 (or_1_out[0], and_1_out, and_2_out, and_3_out);
  or or_2 (or_1_out[1], and_4_out, and_5_out, and_6_out, and_7_out);
  or or_3 (or_1_out[2], and_8_out, and_9_out, and_10_out);
  Register #(.width(3)) register_1 (.D(or_1_out), .en(1'b1), .Q({_2, _1, _0}), .clk(Clock), .clr(Reset));
  and and_11 (and_11_out, _2, _0);
  and and_12 (and_12_out, _0, _1);
  and and_13 (and_13_out, ~_2, ~_1, ~_0);  // AND_Gate
  and and_14 (and_14_out, _1, _0);
  and and_15 (and_15_out, _1, _2);
  and and_16 (and_16_out, ~_2, _1);  // AND_Gate
  and and_17 (and_17_out, ~_1, _2);  // AND_Gate
  and and_18 (Z, ~_0, _2);  // AND_Gate
  or or_4 (W, and_11_out, and_12_out, and_13_out);
  or or_5 (X, and_14_out, and_15_out);
  or or_6 (Y, and_16_out, and_17_out);

  // Other names for the same wires on the sheet: CLK = Clock; RST = Reset

  // Notes on the sheet:
  //   My name is:
  //   [HONGRUI ZHENG]
  //   and this is my reduced state machine
endmodule
